# Fritzing sketch DS18S20OneWire (saved by Fritzing 0.9.0b)
breadboards: 1

parts:
  Q1 = NPN-Transistor [package="TO92 [THT]"]
  Q2 = NPN-Transistor [package="TO92 [THT]"]
  R1 = Resistor [tolerance=±5% resistance=4.7k package=THT]
  Parte1 = Arduino Uno (Rev3)

nets:
  N1: Q1.E, Q1.C, Q2.E, Q2.C, Parte1.GND
  N2: Q1.B, Q2.B, R1.Pin_1, Parte1.D10_PWM/SS
  N3: R1.Pin_0, Parte1.5V

notes:
  Slave1Serial.print("Temperature:");
  Slave2
