# Fritzing sketch GY_521_Module (saved by Fritzing 0.9.0b)

parts:
  GY1 = MPU-6050 Board GY-521 [form="♀ (female)" package=THT]
  Parte1 = Arduino Uno (Rev3)

nets:
  N1: GY1.pin1, Parte1.5V
  N2: GY1.pin2, Parte1.GND
  N3: GY1.pin3, Parte1.A5/SCL
  N4: GY1.pin4, Parte1.A4/SDA
  N5: GY1.pin8, Parte1.D2

custom parts:
  MPU-6050 Board GY-521: Acelerometro y Giroscopio MPU-6050 Board GY-521
