# Fritzing sketch HC_SR04 (saved by Fritzing 0.9.0b)

parts:
  Parte1 = Arduino Uno (Rev3)
  Parte2 = SRF05 Ultrasonic Rangefinder

nets:
  N1: Parte1.D8, Parte2.Echo
  N2: Parte1.D9_PWM, Parte2.Trig
  5V: Parte1.5V, Parte2.VCC
  GND: Parte1.GND, Parte2.GND
