# Fritzing sketch LDR (saved by Fritzing 0.9.0b)
breadboards: 1

parts:
  Parte1 = Arduino Uno (Rev3)
  LED1 = LED - 5mm [color="Red (633nm)" package="5 mm [THT]"]
  R1 = Photocell (LDR) [package=THT]
  R2 = Resistor [tolerance=±5% resistance=220 package=THT]
  R3 = Resistor [tolerance=±5% resistance=220 package=THT]

nets:
  N1: Parte1.A5/SCL, R1.pin_1, R3.Pin_0
  N2: Parte1.GND, R2.Pin_1, R3.Pin_1
  N3: Parte1.D3_PWM, LED1.anode
  N4: Parte1.VIN, R1.pin_0
  N5: LED1.cathode, R2.Pin_0
