# Fritzing sketch Control_L298N (saved by Fritzing 0.9.0b)

parts:
  Parte1 = Arduino Uno (Rev3)
  S1 = H-Bridge with L298N
  M1 = DC Motor  # not connected

nets:
  N1: Parte1.D2, S1.ENA
  N2: Parte1.D3_PWM, S1.IN1
  N3: Parte1.5V, S1.rms
  GND: Parte1.GND, S1.GND

custom parts:
  H-Bridge with L298N: h-bridge
