# Fritzing sketch SpeedWithPotentiometer (saved by Fritzing 0.9.0b)

parts:
  Parte1 = Arduino Uno (Rev3)
  RotationSensorDFR1 = RotationSensorDFR0058
  M1 = DC Motor

nets:
  N1: Parte1.A0, RotationSensorDFR1.SIGNAL
  N2: Parte1.D3_PWM, M1.pin_2
  5V: Parte1.5V, RotationSensorDFR1.5V
  GND: Parte1.GND, RotationSensorDFR1.GND, M1.pin_1
